// Logisim project sap-1.circ as structural Verilog
module sap_1 (
  input  in_1,
  input  in_2,
  input  in_3,
  input  in_4,
  input  in_5,
  input  in_6,
  input  in_7,
  input  in_8,
  input  in_9,
  input  Run_Prog,
  input  A0,
  input  A1,
  input  A2,
  input  A3,
  input  in_15,
  input  in_16,
  input  in_17,
  input  in_18,
  input  in_19,
  input  in_20,
  input  in_21,
  input  in_22,
  input  in_23,
  input  in_24,
  input  in_25,
  input  in_26,
  output out_27,
  output out_28,
  output out_29,
  output out_30,
  output out_31,
  output out_32,
  output out_33,
  output out_34,
  output out_35,
  output out_36,
  output out_37,
  output out_38
);

  wire accumulator_a_1_q0, accumulator_a_1_q1, accumulator_a_1_q2, accumulator_a_1_q3, accumulator_a_1_q4,
       accumulator_a_1_q5, accumulator_a_1_q6, accumulator_a_1_q7, CE_N, CLK, CLK_N, clock_1_out,
       clock_2_out, CLR, CLR_N, Cp, Ea, Ei_N, Ep, Eu, GEN_out, HLT_N, instruction_decoder_1_add,
       instruction_decoder_1_lda, instruction_decoder_1_out, instruction_decoder_1_sub,
       instruction_register_1_l0, instruction_register_1_l1, instruction_register_1_l2,
       instruction_register_1_l3, instruction_register_1_l4, instruction_register_1_l5,
       instruction_register_1_l6, instruction_register_1_l7, intruction_register_1_i4,
       intruction_register_1_i5, intruction_register_1_i6, intruction_register_1_i7, La_N, Lb_N, Li_N, Lm_N,
       Lo_N, mar_1_l0, mar_1_l1, mar_1_l2, mar_1_l3, mar_1_r0, mar_1_r1, mar_1_r2, mar_1_r3,
       memory_address_register_1_q0, memory_address_register_1_q1, memory_address_register_1_q2,
       memory_address_register_1_q3, nibble_multiplexer_1_q0, nibble_multiplexer_1_q1,
       nibble_multiplexer_1_q2, nibble_multiplexer_1_q3, not_1_out, output_register_1_q0,
       output_register_1_q1, output_register_1_q2, output_register_1_q3, output_register_1_q4,
       output_register_1_q5, output_register_1_q6, output_register_1_q7, program_counter_1_l0,
       program_counter_1_l1, program_counter_1_l2, program_counter_1_l3, program_counter_2_q0,
       program_counter_2_q1, program_counter_2_q2, program_counter_2_q3, ram_16x8_1_o4_n, ram_16x8_1_o5_n,
       ram_16x8_1_o6_n, ram_16x8_1_o7_n, register_b_1_q0, register_b_1_q1, register_b_1_q2, register_b_1_q3,
       register_b_1_q4, register_b_1_q5, register_b_1_q6, register_b_1_q7, ring_counter_1_t1,
       ring_counter_1_t2, ring_counter_1_t3, ring_counter_1_t4, ring_counter_1_t5, ring_counter_1_t6,
       START_CLEAR_out, Su;

  Clock clock_1 (.out(clock_1_out));
  Button START_CLEAR (.out(START_CLEAR_out));
  LED led_1 (.in(instruction_register_1_l7));
  Clock clock_2 (.out(clock_2_out));
  Clock GEN (.out(GEN_out));
  not not_1 (not_1_out, START_CLEAR_out);
  LED led_2 (.in(program_counter_1_l1));
  LED led_3 (.in(program_counter_1_l3));
  LED led_4 (.in(program_counter_1_l2));
  LED led_5 (.in(mar_1_l1));
  LED led_6 (.in(mar_1_l3));
  LED led_7 (.in(mar_1_l2));
  LED led_8 (.in(instruction_register_1_l5));
  LED led_9 (.in(instruction_register_1_l3));
  LED led_10 (.in(instruction_register_1_l4));
  LED led_11 (.in(instruction_register_1_l6));
  nand nand_1 (CLR_N, START_CLEAR_out, CLR);
  nand nand_2 (CLR, CLR_N, not_1_out);
  LED led_12 (.in(program_counter_1_l0));
  program_counter program_counter_1 (
    .Ep(in_17), .Cp(in_15), .CLK_N(clock_1_out), .CLR_N(in_16), .L0(program_counter_1_l0), .W0(out_27),
    .L1(program_counter_1_l1), .W1(out_28), .L2(program_counter_1_l2), .W2(out_29),
    .L3(program_counter_1_l3), .W3(out_30));
  LED led_13 (.in(mar_1_l0));
  MAR mar_1 (
    .W0(in_19), .W1(in_21), .W2(in_22), .W3(in_23), .CLK(in_20), .Lm_N(in_18), .R0(mar_1_r0), .R1(mar_1_r1),
    .R2(mar_1_r2), .R3(mar_1_r3), .L3(mar_1_l3), .L2(mar_1_l2), .L1(mar_1_l1), .L0(mar_1_l0));
  RAM16x8 ram16x8_1 (
    .A0(mar_1_r0), .A1(mar_1_r1), .A2(mar_1_r2), .A3(mar_1_r3));  // open: O0, O2, O3, O4, O6, O7, CE_N, O1, O5
  LED led_14 (.in(instruction_register_1_l2));
  LED led_15 (.in(instruction_register_1_l1));
  LED led_16 (.in(instruction_register_1_l0));
  instruction_register instruction_register_1 (
    .W0_IN(out_31), .W1_IN(out_32), .W2_IN(out_33), .W3_IN(out_34), .CLK(clock_2_out), .CLR(in_24),
    .W0_IN_2(out_35), .W1_IN_2(out_36), .W2_IN_2(out_37), .W3_IN_2(out_38), .Li_N(in_25), .Ei_N(in_26),
    .L0(instruction_register_1_l0), .L1(instruction_register_1_l1), .L2(instruction_register_1_l2),
    .L3(instruction_register_1_l3), .W0_OUT(out_31), .W1_OUT(out_32), .W2_OUT(out_33), .W3_OUT(out_34),
    .L4(instruction_register_1_l4), .L5(instruction_register_1_l5), .L6(instruction_register_1_l6),
    .L7(instruction_register_1_l7), .W4_OUT(out_35), .W5_OUT(out_36), .W6_OUT(out_37), .W7_OUT(out_38));  // open: I4, I5, I6, I7
  clock clock_3 (.HLT_N(HLT_N), .CLK(CLK), .CLK_N(CLK_N), .GEN(GEN_out));
  memory_address_register memory_address_register_1 (
    .Lm_N(Lm_N), .CLK(CLK), .D0(program_counter_2_q0), .D1(program_counter_2_q1), .D2(program_counter_2_q2),
    .D3(program_counter_2_q3), .Q0(memory_address_register_1_q0), .Q1(memory_address_register_1_q1),
    .Q2(memory_address_register_1_q2), .Q3(memory_address_register_1_q3));
  nibble_multiplexer nibble_multiplexer_1 (
    .S(Run_Prog), .A0(memory_address_register_1_q0), .A1(memory_address_register_1_q1),
    .Q0(nibble_multiplexer_1_q0), .A2(memory_address_register_1_q2), .A3(memory_address_register_1_q3),
    .B0(A0), .B1(A1), .B2(A2), .B3(A3), .Q1(nibble_multiplexer_1_q1), .Q2(nibble_multiplexer_1_q2),
    .Q3(nibble_multiplexer_1_q3));
  program_counter_program_counter program_counter_2 (
    .Cp(Cp), .CLK_N(CLK_N), .CLR_N(CLR_N), .Ep(Ep), .Q0(program_counter_2_q0), .Q1(program_counter_2_q1),
    .Q2(program_counter_2_q2), .Q3(program_counter_2_q3));
  RAM_16x8 ram_16x8_1 (
    .D0(in_2), .D1(in_3), .D2(in_4), .D3(in_5), .D4(in_6), .D5(in_7), .D6(in_8), .D7(in_9),
    .A0(nibble_multiplexer_1_q0), .A1(nibble_multiplexer_1_q1), .A2(nibble_multiplexer_1_q2),
    .A3(nibble_multiplexer_1_q3), .WE_N(in_1), .CE_N(CE_N), .O0_N(program_counter_2_q0),
    .O1_N(program_counter_2_q1), .O2_N(program_counter_2_q2), .O3_N(program_counter_2_q3),
    .O4_N(ram_16x8_1_o4_n), .O5_N(ram_16x8_1_o5_n), .O6_N(ram_16x8_1_o6_n), .O7_N(ram_16x8_1_o7_n));
  // Probe on ram_16x8_1_o5_n
  // Probe on ram_16x8_1_o7_n
  // Probe on ram_16x8_1_o6_n
  // Probe on program_counter_2_q1
  // Probe on program_counter_2_q2
  // Probe on ram_16x8_1_o4_n
  // Probe on program_counter_2_q3
  // Probe on program_counter_2_q0
  accumulator_a accumulator_a_1 (
    .Ea(Ea), .La_N(La_N), .CLK(CLK), .D0(program_counter_2_q0), .D1(program_counter_2_q1),
    .D2(program_counter_2_q2), .D3(program_counter_2_q3), .D4(ram_16x8_1_o4_n), .D5(ram_16x8_1_o5_n),
    .D6(ram_16x8_1_o6_n), .D7(ram_16x8_1_o7_n), .Q0_Z(program_counter_2_q0), .Q1_Z(program_counter_2_q1),
    .Q2_Z(program_counter_2_q2), .Q3_Z(program_counter_2_q3), .Q0(accumulator_a_1_q0),
    .Q1(accumulator_a_1_q1), .Q2(accumulator_a_1_q2), .Q3(accumulator_a_1_q3), .Q4_Z(ram_16x8_1_o4_n),
    .Q5_Z(ram_16x8_1_o5_n), .Q6_Z(ram_16x8_1_o6_n), .Q7_Z(ram_16x8_1_o7_n), .Q4(accumulator_a_1_q4),
    .Q5(accumulator_a_1_q5), .Q6(accumulator_a_1_q6), .Q7(accumulator_a_1_q7));
  register_b_register_b register_b_1 (
    .La_N(Lb_N), .CLK(CLK), .D0(program_counter_2_q0), .D1(program_counter_2_q1), .D2(program_counter_2_q2),
    .D3(program_counter_2_q3), .D4(ram_16x8_1_o4_n), .D5(ram_16x8_1_o5_n), .D6(ram_16x8_1_o6_n),
    .D7(ram_16x8_1_o7_n), .Q0(register_b_1_q0), .Q1(register_b_1_q1), .Q2(register_b_1_q2),
    .Q3(register_b_1_q3), .Q4(register_b_1_q4), .Q5(register_b_1_q5), .Q6(register_b_1_q6),
    .Q7(register_b_1_q7));
  LED L7 (.in(output_register_1_q7));
  output_register_output_register output_register_1 (
    .CLK(CLK), .D0(program_counter_2_q0), .D1(program_counter_2_q1), .D2(program_counter_2_q2),
    .D3(program_counter_2_q3), .D4(ram_16x8_1_o4_n), .D5(ram_16x8_1_o5_n), .D6(ram_16x8_1_o6_n),
    .D7(ram_16x8_1_o7_n), .Q0(output_register_1_q0), .Q1(output_register_1_q1), .Q2(output_register_1_q2),
    .Q3(output_register_1_q3), .Q4(output_register_1_q4), .Q5(output_register_1_q5),
    .Q6(output_register_1_q6), .Q7(output_register_1_q7), .Lo_N(Lo_N));
  intruction_register intruction_register_1 (
    .Ei_N(Ei_N), .Li_N(Li_N), .CLK(CLK), .D0(program_counter_2_q0), .D1(program_counter_2_q1),
    .D2(program_counter_2_q2), .D3(program_counter_2_q3), .D4(ram_16x8_1_o4_n), .D5(ram_16x8_1_o5_n),
    .D6(ram_16x8_1_o6_n), .D7(ram_16x8_1_o7_n), .Q0(program_counter_2_q0), .Q1(program_counter_2_q1),
    .Q2(program_counter_2_q2), .Q3(program_counter_2_q3), .I4(intruction_register_1_i4),
    .I5(intruction_register_1_i5), .I6(intruction_register_1_i6), .I7(intruction_register_1_i7), .CLR_N(CLR_N));
  LED L3 (.in(output_register_1_q3));
  LED L4 (.in(output_register_1_q4));
  LED L5 (.in(output_register_1_q5));
  LED L6 (.in(output_register_1_q6));
  LED L2 (.in(output_register_1_q2));
  LED L1 (.in(output_register_1_q1));
  LED L0 (.in(output_register_1_q0));
  adder_substr adder_substr_1 (
    .Eu(Eu), .A7(accumulator_a_1_q7), .A6(accumulator_a_1_q6), .A5(accumulator_a_1_q5),
    .A4(accumulator_a_1_q4), .A3(accumulator_a_1_q3), .A2(accumulator_a_1_q2), .A1(accumulator_a_1_q1),
    .A0(accumulator_a_1_q0), .B7(register_b_1_q7), .B6(register_b_1_q6), .B5(register_b_1_q5),
    .B4(register_b_1_q4), .B3(register_b_1_q3), .B2(register_b_1_q2), .B1(register_b_1_q1),
    .B0(register_b_1_q0), .S0(program_counter_2_q0), .S1(program_counter_2_q1), .S2(program_counter_2_q2),
    .S3(program_counter_2_q3), .S4(ram_16x8_1_o4_n), .S5(ram_16x8_1_o5_n), .S6(ram_16x8_1_o6_n), .Su(Su),
    .S7(ram_16x8_1_o7_n));
  ring_counter ring_counter_1 (
    .CLK(CLK), .CLR_N(CLR_N), .T1(ring_counter_1_t1), .T2(ring_counter_1_t2), .T3(ring_counter_1_t3),
    .T4(ring_counter_1_t4), .T5(ring_counter_1_t5), .T6(ring_counter_1_t6));
  instruction_decoder instruction_decoder_1 (
    .LDA(instruction_decoder_1_lda), .ADD(instruction_decoder_1_add), .SUB(instruction_decoder_1_sub),
    .OUT(instruction_decoder_1_out), .HLT_N(HLT_N), .I7(intruction_register_1_i7),
    .I6(intruction_register_1_i6), .I5(intruction_register_1_i5), .I4(intruction_register_1_i4));
  control_matrix control_matrix_1 (
    .T6(ring_counter_1_t6), .T5(ring_counter_1_t5), .T4(ring_counter_1_t4), .T3(ring_counter_1_t3),
    .T2(ring_counter_1_t2), .T1(ring_counter_1_t1), .LDA(instruction_decoder_1_lda),
    .ADD(instruction_decoder_1_add), .SUB(instruction_decoder_1_sub), .OUT(instruction_decoder_1_out),
    .Cp(Cp), .Ep(Ep), .Lm_N(Lm_N), .CE_N(CE_N), .Li_N(Li_N), .Ei_N(Ei_N), .La_N(La_N), .Ea(Ea), .Su(Su),
    .Eu(Eu), .Lb_N(Lb_N), .Lo_N(Lo_N));
endmodule

module program_counter (
  input  Ep,
  input  Cp,
  input  CLK_N,
  input  CLR_N,
  output L0,
  output W0,
  output L1,
  output W1,
  output L2,
  output W2,
  output L3,
  output W3
);

  IC_74107 ic_74107_1 (
    .J1(Cp), .CLK1_N(CLK_N), .K1(Cp), .CLR1_N(CLR_N), .J2(Cp), .CLK2_N(L0), .K2(Cp), .CLR2_N(CLR_N), .Q1(L0),
    .Q2(L1));  // open: Q1_N, Q2_N
  IC_74107 ic_74107_2 (
    .J1(Cp), .CLK1_N(L1), .K1(Cp), .CLR1_N(CLR_N), .J2(Cp), .CLK2_N(L2), .K2(Cp), .CLR2_N(CLR_N), .Q1(L2),
    .Q2(L3));  // open: Q1_N, Q2_N
  assign W0 = Ep ? L0 : 1'bz;  // Controlled_Buffer controlled_buffer_1
  assign W1 = Ep ? L1 : 1'bz;  // Controlled_Buffer controlled_buffer_2
  assign W2 = Ep ? L2 : 1'bz;  // Controlled_Buffer controlled_buffer_3
  assign W3 = Ep ? L3 : 1'bz;  // Controlled_Buffer controlled_buffer_4
endmodule

module MAR (
  input  W0,
  input  W1,
  input  W2,
  input  W3,
  input  CLK,
  input  Lm_N,
  output L3,
  output L2,
  output L1,
  output L0,
  output R0,
  output R1,
  output R2,
  output R3
);

  IC_74173 ic_74173_1 (
    .D1(W0), .D2(W1), .D3(W2), .D4(W3), .CLK(CLK), .CE1(Lm_N), .CE2(Lm_N), .CLR(1'b0), .OE1(1'b0),
    .OE2(1'b0), .Q1(L0), .Q2(L1), .Q3(L2), .Q4(L3));
  IC_74157 ic_74157_1 (
    .A1(1'b0), .B1(L0), .A2(1'b0), .B2(L1), .A3(1'b0), .B3(L2), .A4(1'b0), .B4(L3), .S0(1'b1), .OE(1'b0),
    .Y1(R0), .Y2(R1), .Y3(R2), .Y4(R3));
endmodule

module RAM16x8 (
  input  A0,
  input  A1,
  input  A2,
  input  A3,
  input  CE_N,
  output O0,
  output O1,
  output O2,
  output O3,
  output O4,
  output O5,
  output O6,
  output O7
);

  wire and_1_out, and_2_out, not_1_out, not_2_out;
  wire [7:0] controlled_buffer_1_out;

  not not_1 (not_1_out, 1'b1);
  not not_2 (not_2_out, CE_N);
  assign controlled_buffer_1_out = and_1_out ? {8{1'b0}} : 8'bz;  // Controlled_Buffer controlled_buffer_1
  and and_1 (and_1_out, not_1_out, not_2_out);
  RAM #(.addrWidth(4), .bus("asynch")) ram_1 (
    .addr({A3, A2, A1, A0}), .data(controlled_buffer_1_out), .sel(not_2_out), .ld(1'b1));  // open: clr
  assign {O7, O6, O5, O4, O3, O2, O1, O0} = and_2_out ? controlled_buffer_1_out : 8'bz;  // Controlled_Buffer controlled_buffer_2
  and and_2 (and_2_out, 1'b1, not_2_out);
endmodule

module instruction_register (
  input  W0_IN,
  input  W1_IN,
  input  W2_IN,
  input  W3_IN,
  input  CLK,
  input  CLR,
  input  W0_IN_2,
  input  W1_IN_2,
  input  W2_IN_2,
  input  W3_IN_2,
  input  Li_N,
  input  Ei_N,
  output L0,
  output L1,
  output L2,
  output L3,
  output W0_OUT,
  output W1_OUT,
  output W2_OUT,
  output W3_OUT,
  output L4,
  output L5,
  output L6,
  output L7,
  output I4,
  output W4_OUT,
  output I5,
  output W5_OUT,
  output I6,
  output W6_OUT,
  output I7,
  output W7_OUT
);

  wire not_1_out;

  not not_1 (not_1_out, Ei_N);
  IC_74173 ic_74173_1 (
    .D1(W0_IN), .D2(W1_IN), .D3(W2_IN), .D4(W3_IN), .CLK(CLK), .CE1(Li_N), .CE2(Li_N), .CLR(CLR), .OE1(1'b0),
    .OE2(1'b0), .Q1(L0), .Q2(L1), .Q3(L2), .Q4(L3));
  IC_74173 ic_74173_2 (
    .D1(W0_IN_2), .D2(W1_IN_2), .D3(W2_IN_2), .D4(W3_IN_2), .CLK(CLK), .CE1(Li_N), .CE2(Li_N), .CLR(CLR),
    .OE1(1'b0), .OE2(1'b0), .Q1(I4), .Q2(I5), .Q3(I6), .Q4(I7));
  assign W0_OUT = not_1_out ? L0 : 1'bz;  // Controlled_Buffer controlled_buffer_1
  assign W1_OUT = not_1_out ? L1 : 1'bz;  // Controlled_Buffer controlled_buffer_2
  assign W2_OUT = not_1_out ? L2 : 1'bz;  // Controlled_Buffer controlled_buffer_3
  assign W3_OUT = not_1_out ? L3 : 1'bz;  // Controlled_Buffer controlled_buffer_4
  assign W4_OUT = not_1_out ? 1'b0 : 1'bz;  // Controlled_Buffer controlled_buffer_5
  assign W5_OUT = not_1_out ? 1'b0 : 1'bz;  // Controlled_Buffer controlled_buffer_6
  assign W6_OUT = not_1_out ? 1'b0 : 1'bz;  // Controlled_Buffer controlled_buffer_7
  assign W7_OUT = not_1_out ? 1'b0 : 1'bz;  // Controlled_Buffer controlled_buffer_8

  assign L4 = I4;
  assign L5 = I5;
  assign L6 = I6;
  assign L7 = I7;
endmodule
